# Fritzing sketch BlueDisplayBlink (saved by Fritzing 0.9.2b)
breadboards: 1

parts:
  NANO = Arduino Nano (Rev3.0)
  LED10 = LED - 5mm [color="Red (633nm)" package="5 mm [THT]"]
  HC-05 = Bluetooth HC-05 Macho
  D1 = Rectifier Diode [part_number="1N4001 oder BAT 42" package="300 mil [THT]"]
  R1 = Resistor [tolerance=±5% resistance=220 package=THT]

nets:
  N1: NANO.D1/TX, HC-05.TXD
  N2: NANO.D0/RX, D1.anode
  GND: NANO.GND, LED10.cathode, HC-05.GND
  5V: NANO.5V, HC-05.VCC
  N3: NANO.D13/SCK, R1.Pin_0
  N4: LED10.anode, R1.Pin_1
  N5: HC-05.RXD, D1.cathode

notes:
  BLINK

// code stored in the sketch: Blink.ino
/*
  Blink
  
  Schaltet eine LED im Rythmus von einer Sekunde an und aus
  
  Dieses Beispiel aus dem Fritzing Creator Kit: www.fritzing.org/creator-kit.
*/

int led = 13;                   // ganzzahlige Variable led wird deklariert

void setup() {                  // die setup()-Methode wird einmal ausgeführt
  pinMode(led, OUTPUT);     
}

void loop() {                   // die loop()-Methode wird immer wiederholt
  digitalWrite(led, HIGH);      // schaltet die LED ein 
  delay(1000);                  // hält das Programm für 1000 Millisekunden an
  digitalWrite(led, LOW);       // schaltet die LED ab
  delay(1000);                  // hält das Programm für 1000 Millisekunden an
}
